// Logisim project lab4.circ as structural Verilog: 1 circuit, main circuit main
module main (
  input  w,
  input  x,
  input  y,
  input  z,
  output out_5,
  output out_6,
  output out_7,
  output out_8
);

  wire and_1_out, and_2_out, and_3_out, and_4_out, and_5_out, and_6_out, and_7_out, not_1_out, not_2_out,
       not_3_out, not_4_out, or_1_out;

  not not_1 (not_1_out, w);
  not not_2 (not_2_out, x);
  not not_3 (not_3_out, y);
  not not_4 (not_4_out, z);
  and and_1 (and_1_out, x, y);
  and and_2 (and_2_out, z, x);
  and and_3 (and_3_out, not_2_out, y);
  and and_4 (and_4_out, not_2_out, z);
  and and_5 (and_5_out, x, not_3_out, not_4_out);
  and and_6 (and_6_out, not_3_out, not_4_out);
  and and_7 (and_7_out, y, not_4_out);
  or or_1 (or_1_out, y, not_3_out);
  or or_2 (out_5, and_1_out, and_2_out, w);
  or or_3 (out_6, and_3_out, and_4_out, and_5_out);
  or or_4 (out_7, and_6_out, and_7_out);
  and and_8 (out_8, or_1_out, not_4_out);

  // Notes on the sheet:
  //   w'
  //   X'
  //   y'
  //   z'
  //   A = W+XZ+XY
  //   B = X'Z+X'Y+XY'Z'
  //   C = Y'Z'+YZ
  //   D = Z' (Y'+Y)
endmodule
